# Fritzing sketch schematic (saved by Fritzing 0.9.3b)
breadboards: 1

parts:
  Raspberry_Pi_1 = Raspberry Pi 3 [part_number=RPI-3-V1.2]
  U1 = 74HC595 [package="DIP16 [THT]"]
  Q1 = MOSFET-NCHANNEL [package=to-92]
  R1 = Resistor [tolerance=±5% resistance=1k package=THT]
  R2 = Resistor [tolerance=±5% resistance=1k package=THT]
  LED = LED - 3mm [color="Blue (470nm)" package="3 mm [THT]"]
  LED2 = LED - 3mm [color="Blue (470nm)" package="3 mm [THT]"]
  LED3 = LED - 3mm [color="Blue (470nm)" package="3 mm [THT]"]
  LED4 = LED - 3mm [color="Blue (470nm)" package="3 mm [THT]"]
  LED5 = LED - 3mm [color="Blue (470nm)" package="3 mm [THT]"]
  LED6 = LED - 3mm [color="Blue (470nm)" package="3 mm [THT]"]
  LED7 = LED - 3mm [color="Blue (470nm)" package="3 mm [THT]"]
  LED8 = LED - 3mm [color="Blue (470nm)" package="3 mm [THT]"]

nets:
  3V3: Raspberry_Pi_1.3v3, Raspberry_Pi_1.3V3, U1.MR, U1.VCC, R1.Pin_0
  N1: Raspberry_Pi_1.GIPO10, U1.DS
  N2: Raspberry_Pi_1.GIPO11, U1.SH_CP
  GND: Raspberry_Pi_1.GND, U1.GND, U1.OE, Q1.S, R2.Pin_1, LED.cathode, LED2.cathode, LED3.cathode, LED4.cathode, LED5.cathode, LED6.cathode, LED7.cathode, LED8.cathode
  N3: Raspberry_Pi_1.GIPO8, Q1.G, R2.Pin_0
  N4: U1.Q1, LED7.anode
  N5: U1.Q2, LED6.anode
  N6: U1.Q3, LED5.anode
  N7: U1.Q4, LED4.anode
  N8: U1.Q5, LED3.anode
  N9: U1.Q6, LED2.anode
  N10: U1.Q7, LED.anode
  N11: U1.ST_CP, Q1.D, R1.Pin_1
  N12: U1.Q0, LED8.anode
